# Fritzing sketch 555conductivity (saved by Fritzing 0.8.7b)
breadboards: 1

parts:
  U1 = 555 Timer [package="DIP8 [THT]"]
  VCC1 = Battery
  LED1 = LED - 3mm [color="Red (633nm)" package="3 mm [THT]"]
  R3 = Resistor [tolerance=±5% resistance=147 package=THT]
  R1 = Resistor [tolerance=±5% resistance=20k package=THT]
  R2 = Resistor [tolerance=±5% resistance=15k package=THT]  # not connected
  C1 = Capacitor [package=cap-pth-large]
  C2 = Capacitor [package=cap-pth-large]

nets:
  N1: U1.Ground, VCC1.-, R3.Pin_1
  N2: U1.Trigger, U1.Control_Voltage, C2.1
  N3: U1.Output, LED1.anode
  N4: U1.Reset, U1.Vcc_Supply_Voltage, VCC1.+, R1.Pin_0, C1.2, C2.2
  N5: U1.Threshold, C1.1
  N6: U1.Discharge, R1.Pin_1
  N7: LED1.cathode, R3.Pin_0

notes:
  The resistor "R2" here refers to the resistance across two metal probes (e.g. stainless steel screws, depicted here), which are placed in the water sample; to test the circuit, a 15 k Ohm resistor could be used between the metal screws instead.
  555 chip is oriented with pin #1 at top left in this diagram.
  Led blinking frequency (Hz) =1/(0.7*(R1+2*R2)*C1)
  (R in Ohms, C in Farads): The frequency is inversely related to the resistance; so when the resistance R2 is provided by the liquid between probes in a water sample, the frequency is then inversely related to the liquid's resistance -- and thus directly proportionaly to its conductivity (i.e., higher conductivity means lower higher blinking frequency). [Note: instead of an LED, a piezo buzzer could be used to indicate conductivity levels with sound.)
  For tap water with metal screw probes spaced 1 cm apart (yielding a resistance of approx 15 kOhms on a multimeter), I found that C1 = 10uF, C2=0.001uF, and R1 = 20 kOhms yielded a frequency of about 1.5 Hertz.
  If you use a 'low power' 555 chip that has a minimum voltage of 3V, 2 AA batteries will be sufficient; if you use a 'regular' 555 chip, with a 5V minimum, you'll need 4 AA batteries
